# Fritzing sketch fritzingMainBoardSchematic (saved by Fritzing 0.9.9b)

parts:
  IRFZ44N = Basic FET N-Channel [package="TO220 [THT]"]
  IRFZ44N_(fake) = Basic FET N-Channel [package="TO220 [THT]"]
  ESP32_DevBoard_(dual_core) = MH-ET LIVE ESP32 DEVKIT 38 pins
  80mm_24V_Fan = Fan - Ventilador [package=THT]
  24V_to_9V_step_down_converter = RioRand LM2596
  7805 = Voltage Regulator - 5V [package="DPak [SMD]"]
  UART_to_RS485_module = RS485_XY-017 [part_number=XY-017]
  TC4420 = TC4420 [package=dil-08]
  DMX_IN = XLR NC3MAAH [package=nc3maah]
  C1_330nF = Capacitor [package=cap-pth-small2]
  C2_100nf = Capacitor [package=cap-pth-small2]
  R1 = Resistor [package=THT]
  R2 = Resistor [package=THT]
  R3 = Resistor [package=THT]
  R4 = Resistor [package=THT]
  R5 = Resistor [package=THT]
  Fan_indicator_LED = LED - 5mm [color="Red (633nm)" package="5 mm [THT]"]
  R6 = Resistor [package=THT]
  Strobe_indicator_LED = LED - 5mm [color="Red (633nm)" package="5 mm [THT]"]
  R7 = Resistor [package=THT]
  24V_IN = Screw terminal - 2 pins [package=THT]
  Power_LED_GND = Screw terminal - 2 pins [package=THT]
  24V_to_32V_step_up_converter_-_5A_min = 100W 10A POWER BOOSTER STEP UP VOLTAJ YÜKSELTİCİ [package=THT]
  Power_LED = Screw terminal - 2 pins [package=THT]
  24V_6A_SMPS = Header 2 [package=screwterminal-3.5mm-2_lock]

nets:
  N1: IRFZ44N.gate, TC4420.OUTPUT#5
  N2: IRFZ44N.drain, Power_LED_GND.pin2, Power_LED.pin2
  N3: IRFZ44N.source, IRFZ44N_(fake).source, 24V_to_9V_step_down_converter.Pin_2, R5.Pin_1, 24V_IN.pin1, Power_LED_GND.pin1, 24V_to_32V_step_up_converter_-_5A_min.IN-, 24V_to_32V_step_up_converter_-_5A_min.OUT-, 24V_6A_SMPS.1
  N4: IRFZ44N_(fake).gate, R3.Pin_0, R5.Pin_0
  N5: IRFZ44N_(fake).drain, 80mm_24V_Fan.GND, R6.Pin_0
  N6: ESP32_DevBoard_(dual_core).IO25, TC4420.INPUT, R4.Pin_1
  N7: ESP32_DevBoard_(dual_core).IO26, R3.Pin_1
  N8: ESP32_DevBoard_(dual_core).CMD, 24V_to_9V_step_down_converter.Pin_4, 7805.GND, UART_to_RS485_module.GND#0, TC4420.GND#3, C1_330nF.1, C2_100nf.2, R2.Pin_0
  5V: ESP32_DevBoard_(dual_core).5V, 24V_to_9V_step_down_converter.Pin_3, 7805.input_voltage, TC4420.VDD, C1_330nF.2
  N9: ESP32_DevBoard_(dual_core).IO16, UART_to_RS485_module.TXD, R1.Pin_0, R2.Pin_1
  N10: 80mm_24V_Fan.24v, 24V_to_9V_step_down_converter.Pin_1, Fan_indicator_LED.anode, 24V_IN.pin2, 24V_to_32V_step_up_converter_-_5A_min.IN+, 24V_6A_SMPS.2
  N11: 7805.output_voltage, UART_to_RS485_module.VCC, C2_100nf.1, R1.Pin_1
  N12: UART_to_RS485_module.A, DMX_IN.3
  N13: UART_to_RS485_module.B, DMX_IN.2
  N14: UART_to_RS485_module.GND#5, DMX_IN.1
  N15: TC4420.GND#4, R4.Pin_0, Strobe_indicator_LED.cathode
  N16: TC4420.OUTPUT#6, R7.Pin_1
  N17: Fan_indicator_LED.cathode, R6.Pin_1
  N18: Strobe_indicator_LED.anode, R7.Pin_0
  N19: 24V_to_32V_step_up_converter_-_5A_min.OUT+, Power_LED.pin1

custom parts:
  MH-ET LIVE ESP32 DEVKIT 38 pins: http://mh.nodebb.com/topic/2/mh-et-live-esp32-devkit
  Fan - Ventilador: Ventilador de 2 pines, se encuentra comunmente en computadoras de escritorio
  RS485_XY-017: Commercially available RS485 to RS232 TTL Module
  TC4420: 6A High-Speed MOSFET Driver
  Resistor: A generic 5-band resistor (0.25W)
  Resistor: A generic 5-band resistor (0.25W)
  Resistor: A generic 5-band resistor (0.25W)
  Resistor: A generic 5-band resistor (0.25W)
  Resistor: A generic 5-band resistor (0.25W)
  Resistor: A generic 5-band resistor (0.25W)
